// Logisim project newcpu.circ as structural Verilog: 14 circuits, main circuit main
// RESET
module main (
  input  [7:0] in_1,
  input  in_2,
  input  [7:0] in_3,
  input  [7:0] in_4,
  input  [15:0] in_5,
  input  [5:0] in_6,
  input  in_7,
  output [5:0] out_8,
  output [7:0] out_9,
  output [15:0] out_10
);

  wire alu_1_c, alu_1_p, alu_1_v, alu_1_z, button_1_out, button_2_out, button_3_out, button_4_out,
       button_5_out, button_6_out, clDISP, clDISPLATCH, CLK, clWOUT, cpuCLK, d1, d2, d3, d4, d_ff_1_q, nCLK,
       ncpuCLK, pause, uRESET;
  wire [3:0] s1h, s1l, s2h, s2l, s3h, s3l, s4h, s4l;
  wire [7:0] register_1_q, segdisplay_1_hseg;

  Button button_1 (.out(button_1_out));
  Button button_2 (.out(button_2_out));
  Button button_3 (.out(button_3_out));
  Button button_4 (.out(button_4_out));
  cpuclock cpuclock_1 (.clk(CLK), .cpuclk(cpuCLK), .pause(pause), .step(button_3_out));
  toggleswitch toggleswitch_1 (.switch(pause), .clk(CLK), .res(uRESET), .I(button_4_out));  // open: latch
  debounce debounce_1 (.resp(clWOUT), .req(button_1_out), .clk(CLK));
  debounce debounce_2 (.resp(uRESET), .req(button_2_out), .clk(CLK));
  alu alu_1 (
    .res(out_9), .C(alu_1_c), .Z(alu_1_z), .P(alu_1_p), .V(alu_1_v), .A(in_3), .B(in_4), .fn(in_6),
    .cin(in_2), .en(1'b1));
  not not_1 (nCLK, CLK);
  not not_2 (ncpuCLK, cpuCLK);
  LED led_1 (.in(clWOUT));
  LED led_2 (.in(uRESET));
  LED led_3 (.in(alu_1_c));
  LED led_4 (.in(alu_1_z));
  LED led_5 (.in(alu_1_p));
  LED led_6 (.in(alu_1_v));
  LED led_7 (.in(pause));
  ring6 ring6_1 (.Q(out_8), .clr(uRESET), .clk(CLK));
  Button button_5 (.out(button_5_out));
  D_Flip_Flop d_ff_1 (.D(clDISP), .clk(clDISPLATCH), .Q(d_ff_1_q), .reset(uRESET));  // open: Qn, preset
  pcreg pcreg_1 (.Dout(out_10), .Din(in_5), .reset(uRESET), .load(button_5_out), .clk(cpuCLK), .en(in_7));
  Register register_1 (.D(in_1), .en(clWOUT), .clk(CLK), .Q(register_1_q), .clr(uRESET));
  _7_Segment_Display digit4 (
    .g(s4h[3]), .f(s4h[2]), .a(s4h[1]), .b(s4h[0]), .e(s4l[3]), .d(s4l[2]), .c(s4l[1]), .dp(s4l[0]));
  Button button_6 (.out(button_6_out));
  _7_Segment_Display digit3 (
    .g(s3h[3]), .f(s3h[2]), .a(s3h[1]), .b(s3h[0]), .e(s3l[3]), .d(s3l[2]), .c(s3l[1]), .dp(s3l[0]));
  _7_Segment_Display digit2 (
    .g(s2h[3]), .f(s2h[2]), .a(s2h[1]), .b(s2h[0]), .e(s2l[3]), .d(s2l[2]), .c(s2l[1]), .dp(s2l[0]));
  _7_Segment_Display digit1 (
    .g(s1h[3]), .f(s1h[2]), .a(s1h[1]), .b(s1h[0]), .e(s1l[3]), .d(s1l[2]), .c(s1l[1]), .dp(s1l[0]));
  LED led_8 (.in(clDISP));
  toggleswitch toggleswitch_2 (.switch(clDISP), .latch(clDISPLATCH), .clk(CLK), .res(uRESET), .I(button_6_out));
  segdisplay segdisplay_1 (
    .reset(uRESET), .clk(CLK), .value(register_1_q), .sign(1'b0), .en(d_ff_1_q), .anode({d4, d3, d2, d1}),
    .hseg(segdisplay_1_hseg));
  assign {s1h, s1l} = d1 ? segdisplay_1_hseg : 8'bz;  // Controlled_Buffer controlled_buffer_1
  assign {s2h, s2l} = d2 ? segdisplay_1_hseg : 8'bz;  // Controlled_Buffer controlled_buffer_2
  assign {s3h, s3l} = d3 ? segdisplay_1_hseg : 8'bz;  // Controlled_Buffer controlled_buffer_3
  assign {s4h, s4l} = d4 ? segdisplay_1_hseg : 8'bz;  // Controlled_Buffer controlled_buffer_4

  // Other names for the same wires on the sheet: DBUS[7:0] = in_1

  // Notes on the sheet:
  //   OUTPUT REGISTER
endmodule

module ring (
  input  clr,
  input  clk,
  output [3:0] Q
);

  wire q4, q5, q6, q7;

  D_Flip_Flop d_ff_1 (.D(q6), .clk(clk), .Q(q7), .reset(clr));  // open: Qn, preset
  D_Flip_Flop d_ff_2 (.D(q5), .clk(clk), .Q(q6), .reset(clr));  // open: Qn, preset
  D_Flip_Flop d_ff_3 (.D(q4), .clk(clk), .Q(q5), .reset(clr));  // open: Qn, preset
  D_Flip_Flop d_ff_4 (.D(Q[3]), .clk(clk), .Q(q4), .reset(clr));  // open: Qn, preset
  D_Flip_Flop d_ff_5 (.D(Q[2]), .clk(clk), .Q(Q[3]), .reset(clr));  // open: Qn, preset
  D_Flip_Flop d_ff_6 (.D(Q[1]), .clk(clk), .Q(Q[2]), .reset(clr));  // open: Qn, preset
  D_Flip_Flop d_ff_7 (.D(Q[0]), .clk(clk), .Q(Q[1]), .reset(clr));  // open: Qn, preset
  D_Flip_Flop d_ff_8 (.D(Q[3]), .clk(clk), .Q(Q[0]), .preset(clr));  // open: Qn, reset
endmodule

module segdisplay (
  input  reset,
  input  clk,
  input  [7:0] value,
  input  sign,
  input  en,
  output [3:0] anode,
  output [7:0] hseg
);

  wire wclk;
  wire [3:0] register_1_q, ring_1_p3;
  wire [7:0] register_2_q, SEGROM_data;

  not not_1 (wclk, clk);
  ROM #(.addrWidth(13)) SEGROM (.addr({1'b0, ring_1_p3, value}), .data(SEGROM_data));
  // ring ring_1: pin names not known; wires that end beside it: reset, clk, ring_1_p3
  Register #(.width(4)) register_1 (.D(ring_1_p3), .en(en), .clk(wclk), .Q(register_1_q));  // open: clr
  Register register_2 (.D(SEGROM_data), .en(en), .clk(wclk), .Q(register_2_q));  // open: clr
  assign anode = en ? register_1_q : 4'bz;  // Controlled_Buffer controlled_buffer_1
  assign hseg = en ? register_2_q : 8'bz;  // Controlled_Buffer controlled_buffer_2

  // Other names for the same wires on the sheet: clr = reset; sgn = sign

  // Notes on the sheet:
  //   contents of SEGROM (hex, n*v repeats v):
  //   256*0 7e 12 bc b6 d2 e6 ee 32 fe f2 7e 12 bc b6 d2 e6 ee 32 fe f2 7e 12 bc b6 d2 e6 ee 32 fe f2 7e
  //   12 bc b6 d2 e6 ee 32 fe f2 7e 12 bc b6 d2 e6 ee 32 fe f2 7e 12 bc b6 d2 e6 ee 32 fe f2 7e 12 bc b6
  //   d2 e6 ee 32 fe f2 7e 12 bc b6 d2 e6 ee 32 fe f2 7e 12 bc b6 d2 e6 ee 32 fe f2 7e 12 bc b6 d2 e6 ee
  //   32 fe f2 7e 12 bc b6 d2 e6 ee 32 fe f2 7e 12 bc b6 d2 e6 ee 32 fe f2 7e 12 bc b6 d2 e6 ee 32 fe f2
  //   7e 12 bc b6 d2 e6 ee 32 fe f2 7e 12 bc b6 d2 e6 ee 32 fe f2 7e 12 bc b6 d2 e6 ee 32 fe f2 7e 12 bc
  //   b6 d2 e6 ee 32 fe f2 7e 12 bc b6 d2 e6 ee 32 fe f2 7e 12 bc b6 d2 e6 ee 32 fe f2 7e 12 bc b6 d2 e6
  //   ee 32 fe f2 7e 12 bc b6 d2 e6 ee 32 fe f2 7e 12 bc b6 d2 e6 ee 32 fe f2 7e 12 bc b6 d2 e6 ee 32 fe
  //   f2 7e 12 bc b6 d2 e6 ee 32 fe f2 7e 12 bc b6 d2 e6 ee 32 fe f2 7e 12 bc b6 d2 e6 10*0 10*12 10*bc
  //   10*b6 10*d2 10*e6 10*ee 10*32 10*fe 10*f2 10*7e 10*12 10*bc 10*b6 10*d2 10*e6 10*ee 10*32 10*fe
  //   10*f2 10*7e 10*12 10*bc 10*b6 10*d2 6*e6 6*1 10*ff 340*0 100*12 56*bc
endmodule

module debounce (
  input  req,
  input  clk,
  output resp
);

  wire d_ff_1_q, d_ff_1_qn, d_ff_2_qn;

  D_Flip_Flop d_ff_1 (.D(req), .clk(clk), .Q(d_ff_1_q), .Qn(d_ff_1_qn));  // open: preset, reset
  D_Flip_Flop d_ff_2 (.D(d_ff_1_q), .clk(clk), .Qn(d_ff_2_qn));  // open: Q, preset, reset
  D_Flip_Flop d_ff_3 (.D(d_ff_2_qn), .clk(clk), .Qn(resp));  // open: Q, preset, reset
endmodule

module toggleswitch (
  input  I,
  input  clk,
  input  res,
  output switch,
  output latch
);

  wire d_ff_1_q, d_ff_2_qn;

  D_Flip_Flop d_ff_1 (.D(I), .clk(clk), .Q(d_ff_1_q), .reset(res));  // open: Qn, preset
  D_Flip_Flop d_ff_2 (.D(d_ff_2_qn), .clk(d_ff_1_q), .Q(switch), .Qn(d_ff_2_qn), .reset(res));  // open: preset
  D_Flip_Flop d_ff_3 (.D(d_ff_1_q), .clk(clk), .Q(latch), .reset(res));  // open: Qn, preset
endmodule

module alu (
  input  cin,
  input  [7:0] A,
  input  [7:0] B,
  input  en,
  input  [5:0] fn,
  output [7:0] res,
  output C,
  output Z,
  output P,
  output V
);

  wire and_2_out, and_3_out, and_4_out, cia, coa, cos, not_1_out, not_2_out, not_3_out, not_shift,
       Subtract_Function;
  wire [3:0] or_1_out;
  wire [7:0] aunit_s, lunit_res, sunit_res;

  not not_1 (not_1_out, fn[2]);
  not not_2 (not_2_out, fn[3]);
  shiftunit sunit (.res(sunit_res), .cout(cos), .A(A), .sfn(fn[5:4]), .cin(cin));
  logicunit lunit (.Res(lunit_res), .B(B), .A(A), .lfnc(fn[3:0]));
  xnor xnor_1 (not_shift, fn[4], fn[5]);
  and and_1 (Subtract_Function, fn[0], fn[1], not_1_out, not_2_out);
  adderunit aunit (.cout(coa), .S(aunit_s), .B(lunit_res), .A(sunit_res), .cin(cia));
  alures aluflags (.V(or_1_out[3]), .P(or_1_out[2]), .Z(or_1_out[1]), .aMSB(A[7]), .bMSB(B[7]), .ares(aunit_s));
  assign res = en ? aunit_s : 8'bz;  // Controlled_Buffer controlled_buffer_1
  assign {V, P, Z, C} = en ? or_1_out : 4'bz;  // Controlled_Buffer controlled_buffer_2
  and and_2 (and_2_out, not_shift, coa);
  or or_1 (or_1_out[0], and_2_out, and_3_out);
  not not_3 (not_3_out, not_shift);
  and and_3 (and_3_out, not_3_out, cos);
  and and_4 (and_4_out, cos, not_shift);
  or or_2 (cia, Subtract_Function, and_4_out);

  // Other names for the same wires on the sheet: aMSB = A[7]; bMSB = B[7]; enable = en; f0 = fn[0];
  //   lfn[3:0] = fn[3:0]; f1 = fn[1]; f2 = fn[2]; f3 = fn[3]; f4 = fn[4]; sfn[1:0] = fn[5:4]; f5 = fn[5]

  // Notes on the sheet:
  //   The 'NOT B' logic function is used for 'Subtract'
  //   We need to set Carry if this is the case
  //   If we are executing SHR or SHL we need to ignore carry results from ADDER unit
endmodule

module adderunit (
  input  [7:0] A,
  input  [7:0] B,
  input  cin,
  output cout,
  output [7:0] S
);

  wire c0, c1, c2, c3, c4, c5, c6;

  fulladder fulladder_1 (.S(S[0]), .Co(c0), .A(A[0]), .B(B[0]), .Ci(cin));
  fulladder fulladder_2 (.S(S[1]), .Co(c1), .A(A[1]), .B(B[1]), .Ci(c0));
  fulladder fulladder_3 (.S(S[2]), .Co(c2), .A(A[2]), .B(B[2]), .Ci(c1));
  fulladder fulladder_4 (.S(S[3]), .Co(c3), .A(A[3]), .B(B[3]), .Ci(c2));
  fulladder fulladder_5 (.S(S[4]), .Co(c4), .A(A[4]), .B(B[4]), .Ci(c3));
  fulladder fulladder_6 (.S(S[5]), .Co(c5), .A(A[5]), .B(B[5]), .Ci(c4));
  fulladder fulladder_7 (.S(S[6]), .Co(c6), .A(A[6]), .B(B[6]), .Ci(c5));
  fulladder fulladder_8 (.S(S[7]), .Co(cout), .A(A[7]), .B(B[7]), .Ci(c6));

  // Other names for the same wires on the sheet: c7 = cout
endmodule

module logicunit (
  input  [7:0] B,
  input  [7:0] A,
  input  [3:0] lfnc,
  output [7:0] Res
);

  wire en;

  Multiplexer #(.select(2)) multiplexer_1 (
    .in0(lfnc[0]), .in1(lfnc[1]), .in2(lfnc[2]), .in3(lfnc[3]), .out(Res[0]), .sel({B[0], A[0]}), .en(en));
  Multiplexer #(.select(2)) multiplexer_2 (
    .in0(lfnc[0]), .in1(lfnc[1]), .in2(lfnc[2]), .in3(lfnc[3]), .out(Res[1]), .sel({B[1], A[1]}), .en(en));
  Multiplexer #(.select(2)) multiplexer_3 (
    .in0(lfnc[0]), .in1(lfnc[1]), .in2(lfnc[2]), .in3(lfnc[3]), .out(Res[2]), .sel({B[2], A[2]}), .en(en));
  Multiplexer #(.select(2)) multiplexer_4 (
    .in0(lfnc[0]), .in1(lfnc[1]), .in2(lfnc[2]), .in3(lfnc[3]), .out(Res[3]), .sel({B[3], A[3]}), .en(en));
  Multiplexer #(.select(2)) multiplexer_5 (
    .in0(lfnc[0]), .in1(lfnc[1]), .in2(lfnc[2]), .in3(lfnc[3]), .out(Res[4]), .sel({B[4], A[4]}), .en(en));
  Multiplexer #(.select(2)) multiplexer_6 (
    .in0(lfnc[0]), .in1(lfnc[1]), .in2(lfnc[2]), .in3(lfnc[3]), .out(Res[5]), .sel({B[5], A[5]}), .en(en));
  Multiplexer #(.select(2)) multiplexer_7 (
    .in0(lfnc[0]), .in1(lfnc[1]), .in2(lfnc[2]), .in3(lfnc[3]), .out(Res[6]), .sel({B[6], A[6]}), .en(en));
  Multiplexer #(.select(2)) multiplexer_8 (
    .in0(lfnc[0]), .in1(lfnc[1]), .in2(lfnc[2]), .in3(lfnc[3]), .out(Res[7]), .sel({B[7], A[7]}), .en(en));

  // Other names for the same wires on the sheet: fnc[3:0] = lfnc; r0 = Res[0]; r1 = Res[1]; r2 = Res[2]; r3 = Res[3];
  //   r4 = Res[4]; r5 = Res[5]; r6 = Res[6]; r7 = Res[7]

  // Notes on the sheet:
  //   LOGIC Units Made out of MUXes
  //   0xa          A
  //   0xc          B
  //   0x8          AND
  //   0xe          OR
  //   0x6          XOR
  //   0x1          NOR
  //   0xf          255
  //   lfnc         Logic Function
  //   0x7          NAND
  //   0x3          NOT B
  //   0x5          NOT A
  //   0x0         Zero (0)
endmodule

module shiftunit (
  input  [7:0] A,
  input  [1:0] sfn,
  input  cin,
  output [7:0] res,
  output cout
);

  wire en;

  Multiplexer #(.select(2)) multiplexer_1 (
    .in0(A[0]), .in1(A[1]), .in2(cin), .in3(1'b0), .out(res[0]), .sel(sfn), .en(en));
  Multiplexer #(.select(2)) multiplexer_2 (
    .in0(A[4]), .in1(A[5]), .in2(A[3]), .in3(1'b0), .out(res[4]), .sel(sfn), .en(en));
  Multiplexer #(.select(2)) multiplexer_3 (
    .in0(A[1]), .in1(A[2]), .in2(A[0]), .in3(1'b0), .out(res[1]), .sel(sfn), .en(en));
  Multiplexer #(.select(2)) multiplexer_4 (
    .in0(A[5]), .in1(A[6]), .in2(A[4]), .in3(1'b0), .out(res[5]), .sel(sfn), .en(en));
  Multiplexer #(.select(2)) multiplexer_5 (
    .in0(cin), .in1(A[0]), .in2(A[7]), .in3(1'b0), .out(cout), .sel(sfn), .en(en));
  Multiplexer #(.select(2)) multiplexer_6 (
    .in0(A[2]), .in1(A[3]), .in2(A[1]), .in3(1'b0), .out(res[2]), .sel(sfn), .en(en));
  Multiplexer #(.select(2)) multiplexer_7 (
    .in0(A[6]), .in1(A[7]), .in2(A[5]), .in3(1'b0), .out(res[6]), .sel(sfn), .en(en));
  Multiplexer #(.select(2)) multiplexer_8 (
    .in0(A[3]), .in1(A[4]), .in2(A[2]), .in3(1'b0), .out(res[3]), .sel(sfn), .en(en));
  Multiplexer #(.select(2)) multiplexer_9 (
    .in0(A[7]), .in1(cin), .in2(A[6]), .in3(1'b0), .out(res[7]), .sel(sfn), .en(en));

  // Other names for the same wires on the sheet: r0 = res[0]; r1 = res[1]; r2 = res[2]; r3 = res[3]; r4 = res[4];
  //   r5 = res[5]; r6 = res[6]; r7 = res[7]; sfnc[1:0] = sfn

  // Notes on the sheet:
  //   sfnc         Shift Function
  //   b00          no change
  //   b01          Shift Right
  //   b10          Shift Left
  //   b11          Clear
endmodule

module fulladder (
  input  A,
  input  B,
  input  Ci,
  output S,
  output Co
);

  wire and_1_out, and_2_out, and_3_out, or_1_out, xor_1_out;

  xor xor_1 (xor_1_out, A, B);
  and and_1 (and_1_out, A, B);
  and and_2 (and_2_out, A, Ci);
  and and_3 (and_3_out, B, Ci);
  or or_1 (or_1_out, and_1_out, and_2_out);
  xor xor_2 (S, xor_1_out, Ci);
  or or_2 (Co, or_1_out, and_3_out);

  // Notes on the sheet:
  //   Full 1-bit Adder (carry In, A, B) --> (S(um), carry out)
endmodule

module alures (
  input  [7:0] ares,
  input  aMSB,
  input  bMSB,
  output Z,
  output P,
  output V
);

  wire or_1_out, or_2_out, or_3_out, or_4_out, or_5_out, or_6_out, xor_1_out, xor_2_out, xor_3_out,
       xor_4_out, xor_5_out, xor_6_out, xor_7_out, xor_8_out;

  xor xor_1 (xor_1_out, aMSB, ares[7]);
  xor xor_2 (xor_2_out, ares[7], bMSB);
  and and_1 (V, xor_1_out, xor_2_out);
  or or_1 (or_1_out, ares[7], ares[6]);
  or or_2 (or_2_out, ares[5], ares[4]);
  or or_3 (or_3_out, ares[3], ares[2]);
  or or_4 (or_4_out, ares[1], ares[0]);
  xor xor_3 (xor_3_out, ares[7], ares[6]);
  xor xor_4 (xor_4_out, ares[5], ares[4]);
  xor xor_5 (xor_5_out, ares[3], ares[2]);
  xor xor_6 (xor_6_out, ares[1], ares[0]);
  or or_5 (or_5_out, or_1_out, or_2_out);
  or or_6 (or_6_out, or_3_out, or_4_out);
  xor xor_7 (xor_7_out, xor_3_out, xor_4_out);
  xor xor_8 (xor_8_out, xor_5_out, xor_6_out);
  nor nor_1 (Z, or_5_out, or_6_out);
  xor xor_9 (P, xor_7_out, xor_8_out);

  // Other names for the same wires on the sheet: r0 = ares[0]; r1 = ares[1]; r2 = ares[2]; r3 = ares[3]; r4 = ares[4];
  //   r5 = ares[5]; r6 = ares[6]; r7 = ares[7]; Overflow = V; ParityOdd = P; Zero = Z
endmodule

module cpuclock (
  input  pause,
  input  step,
  output clk,
  output cpuclk
);

  wire and_1_out, and_2_out, d_ff_1_q, d_ff_1_qn, d_ff_2_qn, d_ff_3_qn, not_1_out, undriven, undriven_2;

  Clock clock_1 (.out(clk));
  D_Flip_Flop d_ff_1 (.D(undriven), .clk(undriven_2), .Q(d_ff_1_q), .Qn(d_ff_1_qn));  // open: preset, reset
  D_Flip_Flop d_ff_2 (.D(d_ff_1_q), .clk(undriven_2), .Qn(d_ff_2_qn));  // open: Q, preset, reset
  not not_1 (not_1_out, pause);
  D_Flip_Flop d_ff_3 (.D(d_ff_2_qn), .clk(undriven_2), .Qn(d_ff_3_qn));  // open: Q, preset, reset
  and and_1 (and_1_out, clk, not_1_out);
  and and_2 (and_2_out, pause, step);
  or or_1 (cpuclk, and_1_out, and_2_out);

  // Other names for the same wires on the sheet: MAINCLK = clk
endmodule

module ring6 (
  input  clr,
  input  clk,
  output [5:0] Q
);

  wire q6, q7;

  D_Flip_Flop d_ff_1 (.D(q6), .clk(clk), .Q(q7), .reset(clr));  // open: Qn, preset
  D_Flip_Flop d_ff_2 (.D(Q[5]), .clk(clk), .Q(q6), .reset(clr));  // open: Qn, preset
  D_Flip_Flop d_ff_3 (.D(Q[4]), .clk(clk), .Q(Q[5]), .reset(clr));  // open: Qn, preset
  D_Flip_Flop d_ff_4 (.D(Q[3]), .clk(clk), .Q(Q[4]), .reset(clr));  // open: Qn, preset
  D_Flip_Flop d_ff_5 (.D(Q[2]), .clk(clk), .Q(Q[3]), .reset(clr));  // open: Qn, preset
  D_Flip_Flop d_ff_6 (.D(Q[1]), .clk(clk), .Q(Q[2]), .reset(clr));  // open: Qn, preset
  D_Flip_Flop d_ff_7 (.D(Q[0]), .clk(clk), .Q(Q[1]), .reset(clr));  // open: Qn, preset
  D_Flip_Flop d_ff_8 (.D(Q[5]), .clk(clk), .Q(Q[0]), .preset(clr));  // open: Qn, reset
endmodule

module pcreg (
  input  reset,
  input  load,
  input  clk,
  input  [15:0] Din,
  input  en,
  output [15:0] Dout
);

  wire [15:0] counter_1_q;

  Counter #(.max('hffff), .width(16)) counter_1 (
    .clr(reset), .load(load), .up(1'b1), .count(1'b1), .clk(clk), .D(Din), .Q(counter_1_q));  // open: carry
  assign Dout = en ? counter_1_q : 16'bz;  // Controlled_Buffer controlled_buffer_1
endmodule
